# Fritzing sketch TA (saved by Fritzing 0.9.3b)
breadboards: 1

parts:
  A2 = RS-Pro 92-4535 door lock
  MFRC522 = RFID-RC522-v2
  Mod2 = KY-019 5V Relay Module [package="Breakout board"]
  R2 = Resistor [tolerance=±5% resistance=220 package="2512 [SMD]"]
  R3 = Resistor [tolerance=±5% resistance=220 package="2512 [SMD]"]
  LED3 = LED - 5mm [color="Red (633nm)" package="5 mm [THT]"]
  LED4 = LED - 5mm [color="Red (633nm)" package="5 mm [THT]"]  # not connected
  LED5 = LED - 5mm [color="Red (633nm)" package="5 mm [THT]"]  # not connected
  LED7 = Green LED - Rect 5x2x7mm [package="5x2x7 mm [THT]"]
  R1 = Resistor [tolerance=±5% resistance=220 package="0402 [SMD]"]
  ESP8266 = NodeMCU V1.0
  Part3 = sensor_biometrico

nets:
  N1: A2.pin5, Mod2.Common
  N2: A2.pin6, Mod2.NC
  N3: MFRC522.SDA, ESP8266.D4
  N4: MFRC522.SCK, ESP8266.D5
  N5: MFRC522.MOSI, ESP8266.D7
  N6: MFRC522.MISO, ESP8266.D6
  GND: MFRC522.GND, Mod2.S, R2.Pin_1, R3.Pin_1, LED3.cathode, LED7.cathode, R1.Pin_1, ESP8266.GND, Part3.GND
  N7: MFRC522.RST, ESP8266.D3
  3.3V: MFRC522.3.3V, R1.Pin_0, ESP8266.3V3, ESP8266.SD2, Part3.VCC
  N8: Mod2.+, ESP8266.SD3
  N9: Mod2.-, ESP8266.Vin
  N10: R2.Pin_0, LED7.anode, ESP8266.D0
  N11: R3.Pin_0, LED3.anode, ESP8266.D8
  N12: ESP8266.D1, Part3.RX
  N13: ESP8266.D2, Part3.TX

custom parts:
  RS-Pro 92-4535 door lock: RS-Pro 92-4535 door lock.
  RFID-RC522-v2: A simple China made RFID-RC522 Reader; do check the pin labels, as this is a MFRC522 based clone.
  KY-019 5V Relay Module: KY-019 5V Relay module, used to control AC circuits. (Special thanks to vanepp for fixing the PCB holes and other errors)
  Green LED - Rect 5x2x7mm: A generic rectangular green LED (~1.8V) 5mm x 2mm x 7mm
  NodeMCU V1.0: ESP8266 based NodeMCU
  sensor_biometrico: Adafruit Optical Fingerprint Sensor
